# Fritzing sketch Bazen (saved by Fritzing 0.9.3b)
circuit board: 7.3cm x 6cm

parts:
  5V = Screw terminal - 2 pins [package=THT]
  Arudino_NANO = Arduino Nano (Rev3.0)
  4k7 = Resistor [tolerance=±5% resistance=220 package=THT]
  470 = Resistor [tolerance=±5% resistance=220 package=THT]
  470_2 = Resistor [tolerance=±5% resistance=220 package=THT]
  470_3 = Resistor [tolerance=±5% resistance=220 package=THT]
  TEMP = male alternating pin header, 3 pins [form="♂ (male)"]
  470_4 = Resistor [tolerance=±5% resistance=220 package=THT]
  5V_2 = Screw terminal - 2 pins [package=THT]
  5V_3 = Screw terminal - 2 pins [package=THT]
  A2_A3 = Screw terminal - 2 pins [package=THT]
  SDA/SCL = Screw terminal - 2 pins [package=THT]
  VIN_5-12V = screw terminal, 2 pins
  5V/GND = female pin header, 2 pins [form="♀ (female)"]
  SCL/SDA = female pin header, 2 pins [form="♀ (female)"]
  NC = female pin header, 2 pins [form="♀ (female)"]  # not connected
  A0_A1 = Screw terminal - 2 pins [package=THT]
  LED3 = LED - 5mm [color="Red (633nm)" package="5 mm [THT]"]
  LED2 = LED - 5mm [color="Red (633nm)" package="5 mm [THT]"]
  LED1 = LED - 5mm [color="Red (633nm)" package="5 mm [THT]"]
  DUO_LED = DUO LED RG [package="5 mm [THT]"]
  S1 = Pushbutton [package="[THT]"]
  S2 = Pushbutton [package="[THT]"]
  S3 = Pushbutton [package="[THT]"]
  S4 = Pushbutton [package="[THT]"]
  +_5V_- = Screw terminal - 2 pins [package=THT]

nets:
  N1: 5V.pin1, Arudino_NANO.5V, 4k7.Pin_1, TEMP.pin3, 5V_2.pin1, 5V_3.pin1, 5V/GND.pin2, +_5V_-.pin2
  N2: 5V.pin2, Arudino_NANO.GND, TEMP.pin1, 470_4.Pin_1, 5V_2.pin2, 5V_3.pin2, VIN_5-12V.pin1, 5V/GND.pin1, LED3.cathode, LED2.cathode, LED1.cathode, S1.Pin_3, S1.Pin_4, S2.Pin_3, S2.Pin_4, S3.Pin_3, S3.Pin_4, S4.Pin_3, S4.Pin_4, +_5V_-.pin1
  N3: Arudino_NANO.D2, DUO_LED.red_anode
  N4: Arudino_NANO.D3, S1.Pin_1, S1.Pin_2
  N5: Arudino_NANO.D4, S2.Pin_1, S2.Pin_2
  N6: Arudino_NANO.D5, S3.Pin_1, S3.Pin_2
  N7: Arudino_NANO.D6, S4.Pin_1, S4.Pin_2
  N8: Arudino_NANO.D7, 470_3.Pin_0
  N9: Arudino_NANO.D8, 470.Pin_0
  N10: Arudino_NANO.D9, 470_2.Pin_0
  N11: Arudino_NANO.D10, DUO_LED.green_anode
  N12: Arudino_NANO.D11/MOSI, 4k7.Pin_0, TEMP.pin2
  N13: Arudino_NANO.VIN, VIN_5-12V.pin2
  N14: Arudino_NANO.A5, SDA/SCL.pin1, SCL/SDA.pin2
  N15: Arudino_NANO.A4, SDA/SCL.pin2, SCL/SDA.pin1
  N16: Arudino_NANO.A3, A2_A3.pin1
  N17: Arudino_NANO.A2, A2_A3.pin2
  N18: Arudino_NANO.A1, A0_A1.pin1
  N19: Arudino_NANO.A0, A0_A1.pin2
  N20: 470.Pin_1, LED2.anode
  N21: 470_2.Pin_1, LED1.anode
  N22: 470_3.Pin_1, LED3.anode
  N23: 470_4.Pin_0, DUO_LED.common_cathode

notes:
  BazenBot 2018
  USB
  RTC/DS3231
  -  +
  +VIN-
  [  RELAY  ]
  [   LCD   ]
  Temp connector
  Relay connectors'
  Relay power
  Input power 5-12V
  RTC - DS3231 connector
  5V
  SCL/SDA for LCD
